// Logisim project Real_Alu-Gabri-salvo.circ as structural Verilog
module A_And_B (
  input  [7:0] A,
  input  [7:0] B,
  output [7:0] out_3
);

  assign out_3 = A & B;  // AND_Gate and_1, 8 bits wide
endmodule

module A_Or_B (
  input  [7:0] A,
  input  [7:0] B,
  output [7:0] out_3
);

  assign out_3 = A | B;  // OR_Gate or_1, 8 bits wide
endmodule

module Fulladder (
  input  C0,
  input  a,
  input  b,
  output S,
  output C1
);

  wire and_1_out, and_2_out, and_3_out, xor_1_out;

  and and_1 (and_1_out, C0, a);
  and and_2 (and_2_out, a, b);
  and and_3 (and_3_out, C0, b);
  xor xor_1 (xor_1_out, a, b);
  xor xor_2 (S, xor_1_out, C0);
  or or_1 (C1, and_1_out, and_2_out, and_3_out);
endmodule

module adder_4_bits (
  input  a0,
  input  b0,
  input  C0,
  input  a1,
  input  b1,
  input  a2,
  input  b2,
  input  a3,
  input  b3,
  output S0,
  output S1,
  output S2,
  output S3,
  output C
);

  wire fulladder_1_c1, fulladder_2_c1, fulladder_3_c1;

  Fulladder fulladder_1 (.S(S0), .C1(fulladder_1_c1), .C0(C0), .a(a0), .b(b0));
  Fulladder fulladder_2 (.S(S1), .C1(fulladder_2_c1), .C0(fulladder_1_c1), .a(a1), .b(b1));
  Fulladder fulladder_3 (.S(S2), .C1(fulladder_3_c1), .C0(fulladder_2_c1), .a(a2), .b(b2));
  Fulladder fulladder_4 (.S(S3), .C1(C), .C0(fulladder_3_c1), .a(a3), .b(b3));
endmodule

module Adder_8_bit (
);

  adder_4_bits adder_4_bits_1 ();  // open: S0, S1, S2, S3, a1, a3, a0, a2, b1, b2, b3, b0, C0, C
endmodule
